// Logisim project design.circ as structural Verilog: 10 circuits, main circuit main
module main (
  output [6:0] out_1
);

  wire AC_out, analizadorteclado_1_out_4, and_1_out, comparator_1_eq, memoriainstrucciones_1_ready,
       not_1_out, numeroaascii_1_finished, numeroaascii_1_reloj, or_2_out, or_3_out, R;
  wire [6:0] analizadorteclado_1_salida_ascii, numeroaascii_1_salida, or_1_out;
  wire [15:0] memoriainstrucciones_1_output;
  wire [18:0] _1_out;

  numeroAASCII numeroaascii_1 (
    .Entrada(memoriainstrucciones_1_output), .Reset(R), .Enable(memoriainstrucciones_1_ready),
    .Salida(numeroaascii_1_salida), .Reloj(numeroaascii_1_reloj), .Finished(numeroaascii_1_finished));
  Comparator #(.width(7)) comparator_1 (
    .a({7{1'b0}}), .b(numeroaascii_1_salida), .eq(comparator_1_eq));  // open: gt, lt
  not not_1 (not_1_out, comparator_1_eq);
  and and_1 (and_1_out, not_1_out, numeroaascii_1_reloj);
  assign or_1_out = analizadorteclado_1_salida_ascii | numeroaascii_1_salida;  // OR_Gate or_1, 7 bits wide
  or or_2 (or_2_out, numeroaascii_1_finished, _1_out[10]);
  or or_3 (or_3_out, and_1_out, analizadorteclado_1_out_4);
  TTY #(.rows(1), .cols(30)) tty_1 (.data(or_1_out), .clk(or_3_out), .clr(R));  // open: we
  AnalizadorTeclado analizadorteclado_1 (
    .Entrada(_1_out), .Salida_ASCII(analizadorteclado_1_salida_ascii), .Salida_binario(out_1),
    .out_4(analizadorteclado_1_out_4));
  Button _1 (.out(_1_out[0]));
  Button _4 (.out(_1_out[3]));
  Button _7 (.out(_1_out[6]));
  Button AC (.out(AC_out));
  or or_4 (R, _1_out[10], AC_out);
  Button _3 (.out(_1_out[2]));
  Button _2 (.out(_1_out[1]));
  Button _5 (.out(_1_out[4]));
  Button _6 (.out(_1_out[5]));
  Button _9 (.out(_1_out[8]));
  Button _8 (.out(_1_out[7]));
  Button button (.out(_1_out[10]));
  Button _0 (.out(_1_out[9]));
  MemoriaInstrucciones memoriainstrucciones_1 (
    .Entrada(out_1), .Reloj(analizadorteclado_1_out_4), .Reset_mem(AC_out), ._0_leer_1_escribir(or_2_out),
    .Output(memoriainstrucciones_1_output), .Ready(memoriainstrucciones_1_ready));  // open: Procesar
  Button button_2 (.out(_1_out[14]));
  Button button_3 (.out(_1_out[13]));
  Button x (.out(_1_out[12]));
  Button button_4 (.out(_1_out[11]));
  Button button_5 (.out(_1_out[18]));
  Button button_6 (.out(_1_out[17]));
  Button button_7 (.out(_1_out[16]));
  Button x_y (.out(_1_out[15]));
endmodule

module MemoriaInstrucciones (
  input  [6:0] Entrada,
  input  Reloj,
  input  Reset_mem,
  input  _0_leer_1_escribir,
  output Procesar,
  output [15:0] Output,
  output Ready
);

  wire alu_1_out_6, and_1_out, and_2_out, and_3_out, and_4_out, and_5_out, and_6_out, clock_1_out,
       comparator_2_eq, comparator_3_eq, comparator_4_lt, comparator_5_eq, ne, not_1_out, not_2_out,
       not_4_out, not_5_out, not_6_out, not_7_out, or_1_out, or_2_out, si_soy_un_operador_out_2, t_ff_1_qn,
       tunnel, undriven;
  wire [3:0] ram_2_data;
  wire [6:0] adder_1_out, bit_extender_1_out, counter_1_q, register_1_q;
  wire [7:0] counter_2_q;
  wire [15:0] alu_1_out_5, controlled_buffer_2_out, controlled_buffer_3_out, controlled_buffer_4_out,
       controlled_buffer_5_out, controlled_buffer_6_out, decodificadordeinstrucciones_1_salida,
       multiplexer_2_out, ram_1_data, rdi_q;
  wire [19:0] multiplexer_1_out;
  wire [19:4] ram_2_data_2;

  Register #(.width(7), .Select("low")) register_1 (
    .D(Entrada), .Q(register_1_q), .clk(Reloj), .clr(Reset_mem));  // open: en
  or or_1 (or_1_out, _0_leer_1_escribir, Reset_mem);
  Counter #(.width(7), .max('h7f)) counter_1 (
    .Q(counter_1_q), .clk(tunnel), .clr(or_1_out));  // open: load, D, count, carry, preset, down
  decodificadorDeInstrucciones decodificadordeinstrucciones_1 (
    .Reloj(Reloj), .Entrada(register_1_q), .Reset(Reset_mem), .Salida(decodificadordeinstrucciones_1_salida));
  T_Flip_Flop t_ff_1 (
    .clk(_0_leer_1_escribir), .T(1'b1), .Q(Procesar), .Qn(t_ff_1_qn), .reset(Reset_mem));  // open: preset
  Comparator #(.width(7)) comparator_1 (.a(register_1_q), .b(7'b0100000), .eq(tunnel));  // open: gt, lt
  not not_1 (not_1_out, tunnel);
  RAM #(.addrWidth(7), .dataWidth(16), .Select("high")) ram_1 (
    .addr(counter_1_q), .data(ram_1_data), .clk(Reloj), .ld(Procesar), .clr(Reset_mem));  // open: sel
  and and_1 (and_1_out, not_1_out, t_ff_1_qn);
  assign ram_1_data = and_1_out ? decodificadordeinstrucciones_1_salida : 16'bz;  // Controlled_Buffer controlled_buffer_1
  assign controlled_buffer_2_out = Procesar ? ram_1_data : 16'bz;  // Controlled_Buffer controlled_buffer_2
  EsCodigoOperacion si_soy_un_operador (.in_1(ram_1_data), .out_2(si_soy_un_operador_out_2));
  not not_2 (not_2_out, si_soy_un_operador_out_2);
  not not_3 (ne, si_soy_un_operador_out_2);
  assign controlled_buffer_3_out = si_soy_un_operador_out_2 ? ram_1_data : 16'bz;  // Controlled_Buffer controlled_buffer_3
  assign controlled_buffer_4_out = not_2_out ? ram_1_data : 16'bz;  // Controlled_Buffer controlled_buffer_4
  or or_2 (or_2_out, si_soy_un_operador_out_2, not_2_out);
  and and_2 (and_2_out, or_2_out, Reloj);
  Adder #(.width(7)) adder_1 (.a(counter_1_q), .b(bit_extender_1_out), .out(adder_1_out));  // open: cin, cout
  Bit_Extender #(.out_width(7), .\type ("zero")) bit_extender_1 (.in(counter_2_q), .out(bit_extender_1_out));
  Multiplexer #(.width(20), .enable("false")) multiplexer_1 (
    .in0({4'b0000, controlled_buffer_3_out}), .in1({controlled_buffer_4_out, 4'b0011}),
    .out(multiplexer_1_out), .sel(ne));
  RAM #(.addrWidth(7), .dataWidth(20), .bus("separate"), .Select("low")) ram_2 (
    .addr(adder_1_out), .din(multiplexer_1_out), .data({ram_2_data_2, ram_2_data}), .clk(and_2_out),
    .clr(Reset_mem));  // open: str, sel, ld
  not not_4 (not_4_out, comparator_4_lt);
  Comparator #(.width(4)) comparator_2 (.a(ram_2_data), .b(4'b0011), .eq(comparator_2_eq));  // open: gt, lt
  and and_3 (and_3_out, comparator_2_eq, not_4_out);
  assign controlled_buffer_5_out = and_3_out ? ram_2_data_2 : 16'bz;  // Controlled_Buffer controlled_buffer_5
  Comparator #(.width(4)) comparator_3 (.a(ram_2_data), .b(4'b0001), .eq(comparator_3_eq));  // open: gt, lt
  Multiplexer #(.width(16), .enable("false")) multiplexer_2 (
    .in0(controlled_buffer_6_out), .in1(alu_1_out_5), .out(multiplexer_2_out), .sel(not_5_out));
  not not_5 (not_5_out, comparator_4_lt);
  assign controlled_buffer_6_out = and_4_out ? ram_2_data_2 : 16'bz;  // Controlled_Buffer controlled_buffer_6
  and and_4 (and_4_out, comparator_4_lt, comparator_2_eq);
  Counter #(.trigger("falling")) counter_2 (
    .count(not_7_out), .Q(counter_2_q), .clk(and_5_out), .clr(Reset_mem));  // open: load, D, carry, preset, down
  and and_5 (and_5_out, clock_1_out, Procesar);
  Clock clock_1 (.out(clock_1_out));
  Comparator comparator_4 (.a(counter_2_q), .b(8'h1), .lt(comparator_4_lt));  // open: gt, eq
  Register #(.width(16), .trigger("falling"), .Select("low")) rax (
    .D(multiplexer_2_out), .en(not_7_out), .Q(Output), .clk(and_5_out), .clr(Reset_mem));
  Register #(.width(16), .Select("low")) rdi (
    .D(controlled_buffer_5_out), .Q(rdi_q), .clk(and_6_out), .clr(Reset_mem));  // open: en
  and and_6 (and_6_out, and_5_out, not_6_out);
  not not_6 (not_6_out, comparator_4_lt);
  Comparator #(.width(20)) comparator_5 (
    .a({20{1'b0}}), .b({ram_2_data_2, ram_2_data}), .eq(comparator_5_eq));  // open: gt, lt
  ALU alu_1 (
    .Operando_1(Output), .Operando_2(rdi_q), .out_5(alu_1_out_5), .Operador(ram_2_data), .out_6(alu_1_out_6),
    .Reset(Reset_mem));
  not not_7 (not_7_out, alu_1_out_6);
  Controlled_Buffer controlled_buffer_7 (.in(comparator_3_eq), .en(undriven));  // open: out
  and and_7 (Ready, comparator_5_eq, Procesar);

  // Other names for the same wires on the sheet: Reset = Reset_mem

  // Notes on the sheet:
  //   Dato
  //   CODIGO OPERACION
endmodule

module AnalizadorTeclado (
  input  [18:0] Entrada,
  output [6:0] Salida_ASCII,
  output [6:0] Salida_binario,
  output out_4
);

  Register #(.width(19), .Select("low")) register_1 (.D(Entrada), .clk(out_4));  // open: en, Q, clr
  ROM #(.addrWidth(19), .dataWidth(7), .Select("low")) rom_1 (.addr(Entrada), .data(Salida_ASCII));
  ROM #(.addrWidth(19), .dataWidth(7), .Select("low")) rom_2 (.addr(Entrada), .data(Salida_binario));
  or or_1 (out_4, Salida_ASCII[0], Salida_ASCII[1], Salida_ASCII[2], Salida_ASCII[3], Salida_ASCII[4], Salida_ASCII[5], Salida_ASCII[6]);

  // Notes on the sheet:
  //   contents of rom_1 (hex, n*v repeats v):
  //   0 31 32 0 33 0 0 0 34 7*0 35 15*0 36 31*0 37 63*0 38 127*0 39 255*0 30 511*0 3d 1023*0 21 2047*0 2a
  //   4095*0 2b 8191*0 20 16383*0 5e 32767*0 2f 65535*0 2d 131071*0 25
  //   contents of rom_2 (hex, n*v repeats v):
  //   0 1 2 0 3 0 0 0 4 7*0 5 15*0 6 31*0 7 63*0 8 127*0 9 767*0 3d 1023*0 21 2047*0 2a 4095*0 2b 8191*0
  //   20 16383*0 5e 32767*0 2f 65535*0 2d 131071*0 25
endmodule

module Potenciador (
  input  [15:0] Base,
  input  [15:0] Exponente,
  input  Reloj,
  input  reset,
  output [15:0] Salida,
  output Finished
);

  wire and_1_out, comparator_1_eq, comparator_2_eq, comparator_3_eq, comparator_4_eq, comparator_5_eq,
       comparator_6_eq, d_ff_1_q, not_1_out, or_1_out, or_2_out, or_3_out, register_3_q;
  wire [15:0] controlled_buffer_1_out, counter_1_q, multiplexer_1_out, multiplier_1_out, register_1_q,
       register_2_q, register_4_q, register_5_q;

  or or_1 (or_1_out, reset, register_3_q);
  not not_1 (not_1_out, comparator_3_eq);
  Register #(.width(16), .Select("low")) register_1 (
    .D(Exponente), .Q(register_1_q), .clk(Reloj), .clr(or_2_out));  // open: en
  or or_2 (or_2_out, d_ff_1_q, reset);
  Counter #(.width(16), .max('hffff)) counter_1 (
    .Q(counter_1_q), .clk(Reloj), .clr(or_1_out));  // open: load, D, count, carry, preset, down
  Multiplexer #(.width(16), .enable("false")) multiplexer_1 (
    .in0(Base), .in1(multiplier_1_out), .out(multiplexer_1_out), .sel(not_1_out));
  Register #(.width(16), .Select("low")) register_2 (
    .D(multiplexer_1_out), .Q(register_2_q), .clk(Reloj), .clr(reset));  // open: en
  Comparator #(.width(16)) comparator_1 (.a(counter_1_q), .b(Exponente), .eq(comparator_1_eq));  // open: gt, lt
  Comparator #(.width(16)) comparator_2 (.a(register_1_q), .b(counter_1_q), .eq(comparator_2_eq));  // open: gt, lt
  Register #(.width(1), .Select("low")) register_3 (
    .D(comparator_2_eq), .Q(register_3_q), .clk(Reloj));  // open: en, clr
  Comparator #(.width(16)) comparator_3 (.a(counter_1_q), .b({16{1'b0}}), .eq(comparator_3_eq));  // open: gt, lt
  Register #(.width(16), .Select("low")) register_4 (
    .D(controlled_buffer_1_out), .Q(register_4_q), .clk(Reloj), .clr(reset));  // open: en
  assign controlled_buffer_1_out = comparator_1_eq ? Exponente : 16'bz;  // Controlled_Buffer controlled_buffer_1
  Comparator #(.width(16)) comparator_4 (.a(Exponente), .b({16{1'b0}}), .eq(comparator_4_eq));  // open: gt, lt
  Multiplier #(.width(16)) multiplier_1 (.a(register_2_q), .b(Base), .out(multiplier_1_out));  // open: cin, cout
  Comparator #(.width(1)) comparator_5 (.a(register_3_q), .b(1'b1), .eq(comparator_5_eq));  // open: gt, lt
  Comparator #(.width(16)) comparator_6 (.a(register_4_q), .b(Exponente), .eq(comparator_6_eq));  // open: gt, lt
  Multiplexer #(.width(16), .enable("false")) multiplexer_2 (
    .in0(register_5_q), .in1(16'h1), .out(Salida), .sel(comparator_4_eq));
  Register #(.width(16), .Select("low")) register_5 (
    .D(register_2_q), .en(comparator_2_eq), .Q(register_5_q), .clk(Reloj), .clr(or_3_out));
  D_Flip_Flop d_ff_1 (.clk(Reloj), .Q(d_ff_1_q));  // open: D, Qn, preset, reset
  and and_1 (and_1_out, comparator_5_eq, comparator_6_eq);
  or or_3 (or_3_out, d_ff_1_q, reset);
  D_Flip_Flop d_ff_2 (.clk(Reloj), .D(and_1_out), .Q(Finished), .reset(reset));  // open: Qn, preset

  // Other names for the same wires on the sheet: r = reset

  // Notes on the sheet:
  //   Contador
endmodule

module decodificadorDeInstrucciones (
  input  Reloj,
  input  [6:0] Entrada,
  input  Reset,
  output [15:0] Salida
);

  wire comparator_1_gt, comparator_1_lt, comparator_2_eq, d_ff_1_qn, nand_1_out, or_1_out;
  wire [15:0] bit_extender_1_out, multiplexer_1_out, multiplier_1_out, register_1_q;

  D_Flip_Flop d_ff_1 (.clk(Reloj), .D(comparator_1_gt), .Qn(d_ff_1_qn));  // open: Q, preset, reset
  Comparator #(.width(7)) comparator_1 (
    .a(Entrada), .b(7'b0001010), .gt(comparator_1_gt), .lt(comparator_1_lt));  // open: eq
  Comparator #(.width(7)) comparator_2 (.a(Entrada), .b(7'b0100000), .eq(comparator_2_eq));  // open: gt, lt
  assign bit_extender_1_out = {{9{1'b0}}, Entrada};  // Bit_Extender bit_extender_1
  nand nand_1 (nand_1_out, d_ff_1_qn, comparator_1_lt);
  or or_1 (or_1_out, comparator_2_eq, Reset);
  Register #(.width(16), .Select("low")) register_1 (
    .D(Salida), .Q(register_1_q), .clk(Reloj), .clr(or_1_out));  // open: en
  Multiplier #(.width(16)) multiplier_1 (.a(register_1_q), .b(16'ha), .out(multiplier_1_out));  // open: cin, cout
  Multiplexer #(.width(16), .enable("false")) multiplexer_1 (
    .in0(multiplier_1_out), .in1({16{1'b0}}), .out(multiplexer_1_out), .sel(nand_1_out));
  Adder #(.width(16)) adder_1 (.a(multiplexer_1_out), .b(bit_extender_1_out), .out(Salida));  // open: cin, cout

  // Notes on the sheet:
  //   Estados:
  //   0- Número
  //   1- Operador
endmodule

module ALU (
  input  [15:0] Operando_1,
  input  [15:0] Operando_2,
  input  [3:0] Operador,
  input  Reset,
  output [15:0] out_5,
  output out_6
);

  wire and_1_out, and_2_out, clock_1_out, controlled_buffer_1_out, controlled_buffer_2_out,
       controlled_buffer_3_out, controlled_buffer_4_out, decoder_1_out1, decoder_1_out3, decoder_1_out10,
       decoder_1_out11, decoder_1_out13, decoder_1_out14, decoder_1_out15, factorial_1_finished, or_1_out,
       or_2_out, or_3_out, or_4_out, potenciador_1_finished, t_ff_1_qn;
  wire [15:0] adder_1_out, divider_1_out, factorial_1_salida, multiplexer_1_out, multiplier_1_out,
       potenciador_1_salida, register_1_q, subtractor_1_out;

  Clock clock_1 (.out(clock_1_out));
  assign controlled_buffer_1_out = decoder_1_out1 ? clock_1_out : 1'bz;  // Controlled_Buffer controlled_buffer_1
  assign controlled_buffer_2_out = decoder_1_out14 ? clock_1_out : 1'bz;  // Controlled_Buffer controlled_buffer_2
  Adder #(.width(16)) adder_1 (.a(Operando_1), .b(Operando_2), .out(adder_1_out));  // open: cin, cout
  Factorial factorial_1 (
    .Entrada(Operando_1), .Reloj(controlled_buffer_1_out), .Salida(factorial_1_salida),
    .Finished(factorial_1_finished), .Reset(Reset));
  Subtractor #(.width(16)) subtractor_1 (.a(Operando_1), .b(Operando_2), .out(subtractor_1_out));  // open: bin, bout
  Multiplier #(.width(16)) multiplier_1 (.a(Operando_1), .b(Operando_2), .out(multiplier_1_out));  // open: cin, cout
  Divider #(.width(16)) divider_1 (.a(Operando_1), .b(Operando_2), .out(divider_1_out));  // open: upper, rem
  Potenciador potenciador_1 (
    .Base(Operando_1), .Exponente(Operando_2), .Reloj(controlled_buffer_2_out),
    .Salida(potenciador_1_salida), .Finished(potenciador_1_finished), .reset(Reset));
  Multiplexer #(.select(4), .width(16), .enable("false")) multiplexer_1 (
    .in1(factorial_1_salida), .in10(multiplier_1_out), .in11(adder_1_out), .in13(subtractor_1_out),
    .in14(potenciador_1_salida), .in15(divider_1_out), .out(multiplexer_1_out), .sel(Operador));  // open: in0, in2, in3, in4, in5, in6, in7, in8, in9, in12
  Decoder #(.select(4), .enable("false")) decoder_1 (
    .out1(decoder_1_out1), .out3(decoder_1_out3), .out10(decoder_1_out10), .out11(decoder_1_out11),
    .out13(decoder_1_out13), .out14(decoder_1_out14), .out15(decoder_1_out15), .sel(Operador));  // open: out0, out2, out4, out5, out6, out7, out8, out9, out12
  Register #(.width(16), .Select("low")) register_1 (
    .D(multiplexer_1_out), .Q(register_1_q), .clk(clock_1_out));  // open: en, clr
  or or_1 (or_1_out, decoder_1_out10, decoder_1_out11, decoder_1_out13, decoder_1_out15);
  and and_1 (and_1_out, decoder_1_out1, factorial_1_finished);
  and and_2 (and_2_out, decoder_1_out14, potenciador_1_finished);
  Multiplexer #(.width(16), .enable("false")) multiplexer_2 (
    .in0(register_1_q), .in1(Operando_1), .out(out_5), .sel(decoder_1_out3));
  or or_2 (or_2_out, decoder_1_out10, decoder_1_out11, decoder_1_out1, decoder_1_out14, decoder_1_out15, decoder_1_out13);
  assign controlled_buffer_3_out = t_ff_1_qn ? or_2_out : 1'bz;  // Controlled_Buffer controlled_buffer_3
  assign controlled_buffer_4_out = out_6 ? or_3_out : 1'bz;  // Controlled_Buffer controlled_buffer_4
  or or_3 (or_3_out, or_1_out, and_1_out, and_2_out);
  or or_4 (or_4_out, controlled_buffer_3_out, controlled_buffer_4_out);
  T_Flip_Flop #(.Pre_Clr_Positions("LEGACY")) t_ff_1 (
    .clk(clock_1_out), .T(or_4_out), .Q(out_6), .Qn(t_ff_1_qn), .reset(Reset));  // open: preset

  // Notes on the sheet:
  //   1011 SUMA
  //   1101 RESTA
  //   1111 Division
  //   0001 Factorial
  //   1010 Multiplicacion
  //   1110 Exponente
endmodule

module Convertidor7bitAsciiA4bits (
  input  [15:0] in_1,
  output [3:0] out_2
);


  assign out_2 = in_1[3:0];

  // Notes on the sheet:
  //   1011 SUMA
  //   1101 RESTA
  //   1010 Multiplicacion
  //   1111 Division
  //   1110 Exponente
  //   0001 Factorial
endmodule

module EsCodigoOperacion (
  input  [15:0] in_1,
  output out_2
);

  wire comparator_1_eq, comparator_2_eq, comparator_3_eq, comparator_4_eq, comparator_5_eq, comparator_6_eq;

  Comparator #(.width(16)) comparator_1 (.a(in_1), .b(16'h2b), .eq(comparator_1_eq));  // open: gt, lt
  Comparator #(.width(16)) comparator_2 (.a(in_1), .b(16'h2d), .eq(comparator_2_eq));  // open: gt, lt
  Comparator #(.width(16)) comparator_3 (.a(in_1), .b(16'h2a), .eq(comparator_3_eq));  // open: gt, lt
  Comparator #(.width(16)) comparator_4 (.a(in_1), .b(16'h2f), .eq(comparator_4_eq));  // open: gt, lt
  Comparator #(.width(16)) comparator_5 (.a(in_1), .b(16'h21), .eq(comparator_5_eq));  // open: gt, lt
  Comparator #(.width(16)) comparator_6 (.a(in_1), .b(16'h5e), .eq(comparator_6_eq));  // open: gt, lt
  or or_1 (out_2, comparator_1_eq, comparator_2_eq, comparator_3_eq, comparator_4_eq, comparator_5_eq, comparator_6_eq);
endmodule

module numeroAASCII (
  input  [15:0] Entrada,
  input  Reset,
  input  Enable,
  output [6:0] Salida,
  output Reloj,
  output Finished
);

  wire and_1_out, and_2_out, clock_1_out, comparator_1_eq, comparator_2_gt, not_1_out, or_1_out, t_ff_1_q;
  wire [6:0] ram_1_data, rom_1_data;
  wire [15:0] counter_1_q, divider_1_out, divider_1_rem, multiplexer_1_out, register_1_q;

  Clock clock_1 (.out(clock_1_out));
  and and_1 (and_1_out, clock_1_out, Enable);
  Multiplexer #(.width(16), .enable("false")) multiplexer_1 (
    .in0(divider_1_out), .in1(Entrada), .out(multiplexer_1_out), .sel(comparator_1_eq));
  or or_1 (or_1_out, comparator_1_eq, comparator_2_gt);
  Register #(.width(16), .Select("low")) register_1 (
    .D(multiplexer_1_out), .Q(register_1_q), .clk(and_1_out), .clr(Reset));  // open: en
  Divider #(.width(16)) divider_1 (
    .a(register_1_q), .b(16'ha), .out(divider_1_out), .rem(divider_1_rem));  // open: upper
  Counter #(.width(16), .max('hffff)) counter_1 (
    .Q(counter_1_q), .clk(and_1_out), .clr(Reset), .down(t_ff_1_q));  // open: load, D, count, carry, preset
  T_Flip_Flop t_ff_1 (.clk(or_1_out), .T(1'b1), .Q(t_ff_1_q), .reset(Reset));  // open: Qn, preset
  Comparator #(.width(16)) comparator_1 (.a(counter_1_q), .b({16{1'b0}}), .eq(comparator_1_eq));  // open: gt, lt
  Comparator #(.width(16)) comparator_2 (.a(counter_1_q), .b(16'h5), .gt(comparator_2_gt));  // open: eq, lt
  not not_1 (not_1_out, comparator_1_eq);
  and and_2 (and_2_out, not_1_out, Enable, t_ff_1_q);
  and and_3 (Finished, t_ff_1_q, comparator_1_eq);
  ROM #(.addrWidth(4), .dataWidth(7), .Select("low")) rom_1 (.addr(divider_1_rem[3:0]), .data(rom_1_data));
  RAM #(.addrWidth(16), .dataWidth(7), .bus("separate"), .Select("high")) ram_1 (
    .addr(counter_1_q), .din(rom_1_data), .data(ram_1_data), .clk(and_1_out), .ld(and_2_out), .clr(Reset));  // open: str, sel
  Multiplexer #(.enable("false")) multiplexer_2 (.in0(1'b0), .in1(and_1_out), .out(Reloj), .sel(and_2_out));
  Multiplexer #(.width(7), .enable("false")) multiplexer_3 (
    .in0({7{1'b0}}), .in1(ram_1_data), .out(Salida), .sel(and_2_out));

  // Notes on the sheet:
  //   contents of rom_1 (hex, n*v repeats v):
  //   30 31 32 33 34 35 36 37 38 39
endmodule

module Factorial (
  input  [15:0] Entrada,
  input  Reloj,
  input  Reset,
  output [15:0] Salida,
  output Finished
);

  wire comparator_1_eq, comparator_2_eq, comparator_3_eq, d_ff_1_q, not_1_out, or_1_out, or_2_out;
  wire [15:0] counter_1_q, multiplexer_1_out, multiplier_1_out, register_1_q, register_2_q, register_3_q,
       subtractor_1_out;

  or or_1 (or_1_out, Reset, Finished);
  D_Flip_Flop d_ff_1 (.clk(Reloj), .D(or_1_out), .Q(d_ff_1_q));  // open: Qn, preset, reset
  Multiplexer #(.width(16), .enable("false")) multiplexer_1 (
    .in0(multiplier_1_out), .in1(Entrada), .out(multiplexer_1_out), .sel(comparator_2_eq));
  Comparator #(.width(16)) comparator_1 (.a(Entrada), .b({16{1'b0}}), .eq(comparator_1_eq));  // open: gt, lt
  Register #(.width(16), .Select("low")) register_1 (
    .D(multiplexer_1_out), .Q(register_1_q), .clk(Reloj), .clr(d_ff_1_q));  // open: en
  Counter #(.width(16), .max('hffff)) counter_1 (
    .Q(counter_1_q), .clk(Reloj), .clr(d_ff_1_q));  // open: load, D, count, carry, preset, down
  Multiplexer #(.width(16), .enable("false")) multiplexer_2 (
    .in0(register_2_q), .in1(16'h1), .out(Salida), .sel(comparator_1_eq));
  not not_1 (not_1_out, or_2_out);
  Subtractor #(.width(16)) subtractor_1 (.a(register_3_q), .b(counter_1_q), .out(subtractor_1_out));  // open: bin, bout
  Comparator #(.width(16)) comparator_2 (.a(counter_1_q), .b({16{1'b0}}), .eq(comparator_2_eq));  // open: gt, lt
  Register #(.width(16), .Select("low")) register_2 (
    .D(multiplier_1_out), .en(not_1_out), .Q(register_2_q), .clk(Reloj), .clr(d_ff_1_q));
  Comparator #(.width(16)) comparator_3 (
    .a(counter_1_q), .b(register_3_q), .gt(Finished), .eq(comparator_3_eq));  // open: lt
  Multiplier #(.width(16)) multiplier_1 (
    .a(register_1_q), .b(subtractor_1_out), .out(multiplier_1_out));  // open: cin, cout
  or or_2 (or_2_out, Finished, comparator_3_eq);
  Register #(.width(16), .Select("low")) register_3 (
    .D(Entrada), .en(comparator_2_eq), .Q(register_3_q), .clk(Reloj), .clr(d_ff_1_q));
endmodule
